# Fritzing sketch LamparaAro (saved by Fritzing 0.9.9b)
breadboards: 1

parts:
  WeMos_D1_Mini1 = WeMos D1 Mini
  R1 = Resistor [tolerance=±5% power=0.25 resistance=330 package=THT]
  LED1 = LED - 5mm [color="Blue (505nm)" current=0.030 package="5 mm [THT]"]
  S1 = Toggle Switch [package=THT]
  LED2 = LED - 5mm [color="Red (660nm)" current=0.030 package="5 mm [THT]"]
  R2 = Resistor [tolerance=±5% power=0.25 resistance=330 package=THT]

nets:
  N1: WeMos_D1_Mini1.5V, S1.L2
  N2: WeMos_D1_Mini1.D3, S1.COM, LED2.cathode
  N3: WeMos_D1_Mini1.D4, R1.Pin_1
  N4: WeMos_D1_Mini1.G, LED1.anode, S1.L1, R2.Pin_0
  N5: R1.Pin_0, LED1.cathode
  N6: LED2.anode, R2.Pin_1

// code stored in the sketch: bluetoothLight.ino
char blueToothVal;           //value sent over via bluetooth
char lastValue;              //stores last state of device (on/off)
 
void setup()
{
 Serial.begin(9600); 
 pinMode(13,OUTPUT);
 pinMode(12,INPUT);
}
 
 
void loop()
{
  if(Serial.available())
  {//if there is data being recieved
    blueToothVal=Serial.read(); //read it
  }
  if (blueToothVal=='n')
  {//if value from bluetooth serial is n
    digitalWrite(13,HIGH);            //switch on LED
    if (lastValue!='n')
      Serial.println(F("LED is on")); //print LED is on
    lastValue=blueToothVal;
  }
  else if (blueToothVal=='f')
  {//if value from bluetooth serial is n
    digitalWrite(13,LOW);             //turn off LED
    if (lastValue!='f')
      Serial.println(F("LED is off")); //print LED is on
    lastValue=blueToothVal;
  }
  delay(250);
}
